// Logisim project CPU_Sim.circ as structural Verilog: 14 circuits, main circuit main
module main (
);

  wire Clock, clock_2_out, comparator_1_lt, Control_Unit_b_selector, Control_Unit_write_enable,
       counter_1_carry, not_1_out, Reset, TClock;
  wire [2:0] A, DEC, rom_1_data;
  wire [3:0] B, Control_Unit_op_out, multiplexer_3_out, multiplexer_4_out, priority_encoder_1_p1;
  wire [4:0] MSB;
  wire [5:0] counter_1_q, PC_output;
  wire [6:0] adder_1_out, LSB;
  wire [8:0] Data, multiplexer_1_out, multiplexer_2_out, n9_bit_alu_1_out_20, R0, R1, R2, R3, R4, R5, R6, R7;
  wire [22:19] ram_1_data;

  Register_File Register_File (
    .Write_Enable(Control_Unit_write_enable), .Reset(Reset), ._9_bits_for_writing(n9_bit_alu_1_out_20),
    .Decoder(DEC), .R0(R0), .R1(R1), .R2(R2), .R3(R3), .R4(R4), .R5(R5), .R6(R6), .R7(R7));
  PC PC (.Clock(Clock), .Reset(Reset), .Output(PC_output));
  RAM #(.addrWidth(6), .dataWidth(23), .bus("separate")) ram_1 (
    .addr(PC_output), .data({ram_1_data, DEC, A, B, Data}), .str(1'b0), .clk(Clock), .ld(1'b1));  // open: din, sel, clr
  Clock clock_1 (.out(Clock));
  Multiplexer #(.select(3), .width(9), .enable("false")) multiplexer_1 (
    .in0(R0), .in1(R1), .in2(R2), .in3(R3), .in4(R4), .in5(R5), .in6(R6), .in7(R7), .out(multiplexer_1_out),
    .sel(A));
  Control_Unit Control_Unit (
    .OP_In(ram_1_data), .B_Selector(Control_Unit_b_selector), .OP_Out(Control_Unit_op_out), .Clock(Clock),
    .Write_Enable(Control_Unit_write_enable));
  _9_bit_ALU u_9_bit_alu_1 (
    .B8(multiplexer_2_out[8]), .B7(multiplexer_2_out[7]), .B6(multiplexer_2_out[6]),
    .B5(multiplexer_2_out[5]), .B4(multiplexer_2_out[4]), .B3(multiplexer_2_out[3]),
    .B2(multiplexer_2_out[2]), .B1(multiplexer_2_out[1]), .B0(multiplexer_2_out[0]),
    .A8(multiplexer_1_out[8]), .A7(multiplexer_1_out[7]), .A6(multiplexer_1_out[6]),
    .A5(multiplexer_1_out[5]), .A4(multiplexer_1_out[4]), .A3(multiplexer_1_out[3]),
    .A2(multiplexer_1_out[2]), .A1(multiplexer_1_out[1]), .A0(multiplexer_1_out[0]),
    .Op_Code(Control_Unit_op_out), .out_20(n9_bit_alu_1_out_20));
  Multiplexer #(.select(4), .width(9), .enable("false")) multiplexer_2 (
    .in0(R0), .in1(R1), .in2(R2), .in3(R3), .in4(R4), .in5(R5), .in6(R6), .in7(R7), .in8(Data),
    .out(multiplexer_2_out), .sel(multiplexer_3_out));  // open: in9, in10, in11, in12, in13, in14, in15
  Multiplexer #(.width(4), .enable("false")) multiplexer_3 (
    .in0(B), .in1(priority_encoder_1_p1), .out(multiplexer_3_out), .sel(Control_Unit_b_selector));
  // Priority_Encoder #(.select(4)) priority_encoder_1: pin names not known; wires that end beside it: priority_encoder_1_p1, 1'b1
  TTY #(.rows(33), .cols(1)) tty_1 (.data({2'b10, MSB}), .clk(TClock), .clr(Reset));  // open: we
  TTY #(.rows(33), .cols(1)) tty_2 (.data(LSB), .clk(TClock), .clr(Reset));  // open: we
  Button u_Reset (.out(Reset));
  Counter #(.width(6), .max('h20), .ongoal("stay")) counter_1 (
    .Q(counter_1_q), .carry(counter_1_carry), .clk(TClock), .clr(Reset));  // open: load, D, count
  Multiplexer #(.select(3), .width(9), .disabled(0), .enable("false")) multiplexer_4 (
    .in0(R0), .in1(R1), .in2(R2), .in3(R3), .in4(R4), .in5(R5), .in6(R6), .in7(R7),
    .out({MSB, multiplexer_4_out}), .sel(rom_1_data));
  not not_1 (not_1_out, counter_1_carry);
  Clock clock_2 (.out(clock_2_out));
  and and_1 (TClock, not_1_out, clock_2_out);
  ROM #(.addrWidth(6), .dataWidth(3)) rom_1 (.addr(counter_1_q), .data(rom_1_data));  // open: sel
  // Probe on {3'b011, multiplexer_4_out}
  // Probe on {2'b10, MSB}
  Comparator #(.width(7)) comparator_1 (
    .a(7'b0111001), .b({3'b011, multiplexer_4_out}), .lt(comparator_1_lt));  // open: gt, eq
  // Probe on LSB
  Multiplexer #(.width(7), .disabled(0), .enable("false")) multiplexer_5 (
    .in0({3'b011, multiplexer_4_out}), .in1(adder_1_out), .out(LSB), .sel(comparator_1_lt));
  Adder #(.width(7)) adder_1 (.a({3'b011, multiplexer_4_out}), .b(7'b0000111), .out(adder_1_out));  // open: cin, cout

  // Notes on the sheet:
  //   @0
  //   JA
  //   E5
  //   @0
  //   OF
  //   U5
  //   OF
  //   E5
  //   E5
  //   U4
  //   E5
  //   E5
  //   U4
  //   _F
  //   _F
  //   _F
  //   AF
  //   AF
  //   AF
  //   @0
  //   AE
  //   AE
  //   AE
  //   _E
  //   OF
  //   ^0
  //   J9
  //   P1
  //   R0
  //   R0
  //   ^0
  //   _F
  //   contents of rom_1 (hex, n*v repeats v):
  //   0 0 1 2 3 4 5 6 6 2 3 4 5 6 6 0 1 2 3 4 5 6 6 2 3 4 5 6 6 6 7
endmodule

module _9_bit_ALU (
  input  B8,
  input  B7,
  input  B6,
  input  B5,
  input  B4,
  input  B3,
  input  B2,
  input  B1,
  input  B0,
  input  A8,
  input  A7,
  input  A6,
  input  A5,
  input  A4,
  input  A3,
  input  A2,
  input  A1,
  input  A0,
  input  [3:0] Op_Code,
  output [8:0] out_20
);

  wire [8:0] and_1_c0, full_adder_1_s0, full_adder_2_s0, full_subtractor_1_s0, full_subtractor_2_s0,
       not_1_out, or_1_c0, xor_1_c0;

  AND and_1 (
    .A8(A8), .B8(B8), .A7(A7), .B7(B7), .A6(A6), .B6(B6), .A5(A5), .B5(B5), .A4(A4), .B4(B4), .A3(A3),
    .B3(B3), .A2(A2), .B2(B2), .A1(A1), .B1(B1), .A0(A0), .B0(B0), .C8(and_1_c0[8]), .C7(and_1_c0[7]),
    .C6(and_1_c0[6]), .C5(and_1_c0[5]), .C4(and_1_c0[4]), .C3(and_1_c0[3]), .C2(and_1_c0[2]),
    .C1(and_1_c0[1]), .C0(and_1_c0[0]));
  OR or_1 (
    .A8(A8), .B8(B8), .A7(A7), .B7(B7), .A6(A6), .B6(B6), .A5(A5), .B5(B5), .A4(A4), .B4(B4), .A3(A3),
    .B3(B3), .A2(A2), .B2(B2), .A1(A1), .B1(B1), .A0(A0), .B0(B0), .C8(or_1_c0[8]), .C7(or_1_c0[7]),
    .C6(or_1_c0[6]), .C5(or_1_c0[5]), .C4(or_1_c0[4]), .C3(or_1_c0[3]), .C2(or_1_c0[2]), .C1(or_1_c0[1]),
    .C0(or_1_c0[0]));
  XOR xor_1 (
    .A8(A8), .B8(B8), .A7(A7), .B7(B7), .A6(A6), .B6(B6), .A5(A5), .B5(B5), .A4(A4), .B4(B4), .A3(A3),
    .B3(B3), .A2(A2), .B2(B2), .A1(A1), .B1(B1), .A0(A0), .B0(B0), .C8(xor_1_c0[8]), .C7(xor_1_c0[7]),
    .C6(xor_1_c0[6]), .C5(xor_1_c0[5]), .C4(xor_1_c0[4]), .C3(xor_1_c0[3]), .C2(xor_1_c0[2]),
    .C1(xor_1_c0[1]), .C0(xor_1_c0[0]));
  Full_Adder full_adder_1 (
    .A8(A8), .B8(B8), .A7(A7), .B7(B7), .A6(A6), .B6(B6), .A5(A5), .B5(B5), .A4(A4), .B4(B4), .A3(A3),
    .B3(B3), .A2(A2), .B2(B2), .A1(A1), .B1(B1), .A0(A0), .B0(B0), .C0(1'b0), .S8(full_adder_1_s0[8]),
    .S7(full_adder_1_s0[7]), .S6(full_adder_1_s0[6]), .S5(full_adder_1_s0[5]), .S4(full_adder_1_s0[4]),
    .S3(full_adder_1_s0[3]), .S2(full_adder_1_s0[2]), .S1(full_adder_1_s0[1]), .S0(full_adder_1_s0[0]));
  Full_Subtractor full_subtractor_1 (
    .A8(A8), .B8(B8), .A7(A7), .B7(B7), .A6(A6), .B6(B6), .A5(A5), .B5(B5), .A4(A4), .B4(B4), .A3(A3),
    .B3(B3), .A2(A2), .B2(B2), .A1(A1), .B1(B1), .A0(A0), .B0(B0), .C0(1'b1), .S8(full_subtractor_1_s0[8]),
    .S7(full_subtractor_1_s0[7]), .S6(full_subtractor_1_s0[6]), .S5(full_subtractor_1_s0[5]),
    .S4(full_subtractor_1_s0[4]), .S3(full_subtractor_1_s0[3]), .S2(full_subtractor_1_s0[2]),
    .S1(full_subtractor_1_s0[1]), .S0(full_subtractor_1_s0[0]));
  Full_Adder full_adder_2 (
    .A8(A8), .B8(B8), .A7(A7), .B7(B7), .A6(A6), .B6(B6), .A5(A5), .B5(B5), .A4(A4), .B4(B4), .A3(A3),
    .B3(B3), .A2(A2), .B2(B2), .A1(A1), .B1(B1), .A0(A0), .B0(B0), .C0(1'b0), .S8(full_adder_2_s0[8]),
    .S7(full_adder_2_s0[7]), .S6(full_adder_2_s0[6]), .S5(full_adder_2_s0[5]), .S4(full_adder_2_s0[4]),
    .S3(full_adder_2_s0[3]), .S2(full_adder_2_s0[2]), .S1(full_adder_2_s0[1]), .S0(full_adder_2_s0[0]));
  Full_Subtractor full_subtractor_2 (
    .A8(A8), .B8(B8), .A7(A7), .B7(B7), .A6(A6), .B6(B6), .A5(A5), .B5(B5), .A4(A4), .B4(B4), .A3(A3),
    .B3(B3), .A2(A2), .B2(B2), .A1(A1), .B1(B1), .A0(A0), .B0(B0), .C0(1'b1), .S8(full_subtractor_2_s0[8]),
    .S7(full_subtractor_2_s0[7]), .S6(full_subtractor_2_s0[6]), .S5(full_subtractor_2_s0[5]),
    .S4(full_subtractor_2_s0[4]), .S3(full_subtractor_2_s0[3]), .S2(full_subtractor_2_s0[2]),
    .S1(full_subtractor_2_s0[1]), .S0(full_subtractor_2_s0[0]));
  assign not_1_out = ~{A8, A7, A6, A5, A4, A3, A2, A1, A0};  // NOT_Gate not_1, 9 bits wide
  Multiplexer #(.select(4), .width(9), .enable("false")) multiplexer_1 (
    .in1({A8, A7, A6, A5, A4, A3, A2, A1, A0}), .in2(not_1_out), .in3(and_1_c0), .in4(or_1_c0),
    .in5(xor_1_c0), .in6(full_adder_1_s0), .in7(full_subtractor_1_s0),
    .in8({A7, A6, A5, A4, A3, A2, A1, A0, 1'b0}), .in9({1'b0, A8, A7, A6, A5, A4, A3, A2, A1}),
    .in10({B8, B7, B6, B5, B4, B3, B2, B1, B0}), .in11(full_adder_2_s0), .in12(full_subtractor_2_s0),
    .out(out_20), .sel(Op_Code));  // open: in0, in13, in14, in15
endmodule

module XOR (
  input  A8,
  input  B8,
  input  A7,
  input  B7,
  input  A6,
  input  B6,
  input  A5,
  input  B5,
  input  A4,
  input  B4,
  input  A3,
  input  B3,
  input  A2,
  input  B2,
  input  A1,
  input  B1,
  input  A0,
  input  B0,
  output C8,
  output C7,
  output C6,
  output C5,
  output C4,
  output C3,
  output C2,
  output C1,
  output C0
);

  xor xor_1 (C8, A8, B8);
  xor xor_2 (C7, A7, B7);
  xor xor_3 (C6, A6, B6);
  xor xor_4 (C5, A5, B5);
  xor xor_5 (C4, A4, B4);
  xor xor_6 (C3, A3, B3);
  xor xor_7 (C2, A2, B2);
  xor xor_8 (C1, A1, B1);
  xor xor_9 (C0, A0, B0);
endmodule

module OR (
  input  A8,
  input  B8,
  input  A7,
  input  B7,
  input  A6,
  input  B6,
  input  A5,
  input  B5,
  input  A4,
  input  B4,
  input  A3,
  input  B3,
  input  A2,
  input  B2,
  input  A1,
  input  B1,
  input  A0,
  input  B0,
  output C8,
  output C7,
  output C6,
  output C5,
  output C4,
  output C3,
  output C2,
  output C1,
  output C0
);

  or or_1 (C8, A8, B8);
  or or_2 (C7, A7, B7);
  or or_3 (C6, A6, B6);
  or or_4 (C5, A5, B5);
  or or_5 (C4, A4, B4);
  or or_6 (C3, A3, B3);
  or or_7 (C2, A2, B2);
  or or_8 (C1, A1, B1);
  or or_9 (C0, A0, B0);
endmodule

module AND (
  input  A8,
  input  B8,
  input  A7,
  input  B7,
  input  A6,
  input  B6,
  input  A5,
  input  B5,
  input  A4,
  input  B4,
  input  A3,
  input  B3,
  input  A2,
  input  B2,
  input  A1,
  input  B1,
  input  A0,
  input  B0,
  output C8,
  output C7,
  output C6,
  output C5,
  output C4,
  output C3,
  output C2,
  output C1,
  output C0
);

  and and_1 (C8, A8, B8);
  and and_2 (C7, A7, B7);
  and and_3 (C6, A6, B6);
  and and_4 (C5, A5, B5);
  and and_5 (C4, A4, B4);
  and and_6 (C3, A3, B3);
  and and_7 (C2, A2, B2);
  and and_8 (C1, A1, B1);
  and and_9 (C0, A0, B0);
endmodule

module Register_File (
  input  Reset,
  input  [2:0] Decoder,
  input  [8:0] _9_bits_for_writing,
  input  Write_Enable,
  output [8:0] R0,
  output [8:0] R1,
  output [8:0] R2,
  output [8:0] R3,
  output [8:0] R4,
  output [8:0] R5,
  output [8:0] R6,
  output [8:0] R7
);

  wire Clock_out;
  wire [8:0] demultiplexer_1_out0, demultiplexer_1_out1, demultiplexer_1_out2, demultiplexer_1_out3,
       demultiplexer_1_out4, demultiplexer_1_out5, demultiplexer_1_out6, demultiplexer_1_out7;

  Demultiplexer #(.select(3), .width(9), .tristate("true"), .enable("false")) demultiplexer_1 (
    .out0(demultiplexer_1_out0), .out1(demultiplexer_1_out1), .out2(demultiplexer_1_out2),
    .out3(demultiplexer_1_out3), .out4(demultiplexer_1_out4), .out5(demultiplexer_1_out5),
    .out6(demultiplexer_1_out6), .out7(demultiplexer_1_out7), .in(_9_bits_for_writing), .sel(Decoder));
  Clock Clock (.out(Clock_out));
  Register register_1 (
    .Input(demultiplexer_1_out0), .Clock(Clock_out), .Write_Enable(Write_Enable), .Reset(Reset), .Output(R0));
  Register register_2 (
    .Input(demultiplexer_1_out1), .Clock(Clock_out), .Write_Enable(Write_Enable), .Reset(Reset), .Output(R1));
  Register register_3 (
    .Input(demultiplexer_1_out2), .Clock(Clock_out), .Write_Enable(Write_Enable), .Reset(Reset), .Output(R2));
  Register register_4 (
    .Input(demultiplexer_1_out3), .Clock(Clock_out), .Write_Enable(Write_Enable), .Reset(Reset), .Output(R3));
  Register register_5 (
    .Input(demultiplexer_1_out4), .Clock(Clock_out), .Write_Enable(Write_Enable), .Reset(Reset), .Output(R4));
  Register register_6 (
    .Input(demultiplexer_1_out5), .Clock(Clock_out), .Write_Enable(Write_Enable), .Reset(Reset), .Output(R5));
  Register register_7 (
    .Input(demultiplexer_1_out6), .Clock(Clock_out), .Write_Enable(Write_Enable), .Reset(Reset), .Output(R6));
  Register register_8 (
    .Input(demultiplexer_1_out7), .Clock(Clock_out), .Write_Enable(Write_Enable), .Reset(Reset), .Output(R7));
endmodule

module Register (
  input  [8:0] Input,
  input  Clock,
  input  Write_Enable,
  input  Reset,
  output [8:0] Output
);

  wire and_1_out;

  and and_1 (and_1_out, Clock, Write_Enable);
  D_Flip_Flop d_ff_1 (.clk(and_1_out), .D(Input[0]), .Q(Output[0]), .reset(Reset));  // open: Qn, preset, en
  D_Flip_Flop d_ff_2 (.clk(and_1_out), .D(Input[1]), .Q(Output[1]), .reset(Reset));  // open: Qn, preset, en
  D_Flip_Flop d_ff_3 (.clk(and_1_out), .D(Input[2]), .Q(Output[2]), .reset(Reset));  // open: Qn, preset, en
  D_Flip_Flop d_ff_4 (.clk(and_1_out), .D(Input[3]), .Q(Output[3]), .reset(Reset));  // open: Qn, preset, en
  D_Flip_Flop d_ff_5 (.clk(and_1_out), .D(Input[4]), .Q(Output[4]), .reset(Reset));  // open: Qn, preset, en
  D_Flip_Flop d_ff_6 (.clk(and_1_out), .D(Input[5]), .Q(Output[5]), .reset(Reset));  // open: Qn, preset, en
  D_Flip_Flop d_ff_7 (.clk(and_1_out), .D(Input[6]), .Q(Output[6]), .reset(Reset));  // open: Qn, preset, en
  D_Flip_Flop d_ff_8 (.clk(and_1_out), .D(Input[7]), .Q(Output[7]), .reset(Reset));  // open: Qn, preset, en
  D_Flip_Flop d_ff_9 (.clk(and_1_out), .D(Input[8]), .Q(Output[8]));  // open: Qn, preset, en, reset
endmodule

module PC (
  input  Clock,
  input  Reset,
  output [5:0] Output
);

  wire and_1_out, and_2_out, and_3_out, and_4_out;

  T_Flip_Flop FF0 (.clk(Clock), .T(1'b1), .Q(Output[0]));  // open: Qn, preset, reset, en
  T_Flip_Flop FF1 (.clk(Clock), .T(Output[0]), .Q(Output[1]), .reset(Reset));  // open: Qn, preset, en
  and and_1 (and_1_out, Output[1], Output[0]);
  T_Flip_Flop FF2 (.clk(Clock), .T(and_1_out), .Q(Output[2]), .reset(Reset));  // open: Qn, preset, en
  and and_2 (and_2_out, Output[2], and_1_out);
  T_Flip_Flop FF3 (.clk(Clock), .T(and_2_out), .Q(Output[3]), .reset(Reset));  // open: Qn, preset, en
  T_Flip_Flop FF4 (.clk(Clock), .T(and_3_out), .Q(Output[4]), .reset(Reset));  // open: Qn, preset, en
  and and_3 (and_3_out, Output[3], and_2_out);
  and and_4 (and_4_out, Output[4], and_3_out);
  T_Flip_Flop FF5 (.clk(Clock), .T(and_4_out), .Q(Output[5]), .reset(Reset));  // open: Qn, preset, en
endmodule

module Control_Unit (
  input  [3:0] OP_In,
  input  Clock,
  output [3:0] OP_Out,
  output B_Selector,
  output Write_Enable
);

  wire and_1_out, and_2_out, comparator_1_eq, comparator_1_lt, comparator_2_eq, comparator_2_gt, not_1_out,
       not_2_out, not_3_out, not_4_out, or_1_out, or_2_out, priority_encoder_1_gs, t_ff_1_q;
  wire [3:0] priority_encoder_1_out, priority_encoder_2_out;

  Priority_Encoder #(.select(4)) priority_encoder_1 (
    .in10(1'b1), .out(priority_encoder_1_out), .gs(priority_encoder_1_gs));  // open: in0, in1, in2, in3, in4, in5, in6, in7, in8, in9, in11, in12, in13, in14, in15, en_out, en_in
  Priority_Encoder #(.select(4)) priority_encoder_2 (
    .in12(1'b1), .out(priority_encoder_2_out));  // open: in0, in1, in2, in3, in4, in5, in6, in7, in8, in9, in10, in11, in13, in14, in15, gs, en_out, en_in
  not not_1 (not_1_out, OP_In[0]);
  not not_2 (not_2_out, OP_In[1]);
  not not_3 (not_3_out, OP_In[2]);
  not not_4 (not_4_out, OP_In[3]);
  Comparator #(.width(4), .mode("unsigned")) comparator_1 (
    .a(priority_encoder_1_out), .b(OP_In), .eq(comparator_1_eq), .lt(comparator_1_lt));  // open: gt
  Comparator #(.width(4), .mode("unsigned")) comparator_2 (
    .a(priority_encoder_2_out), .b(OP_In), .gt(comparator_2_gt), .eq(comparator_2_eq));  // open: lt
  and and_1 (and_1_out, OP_In[0], OP_In[1], OP_In[2], OP_In[3]);
  and and_2 (and_2_out, not_1_out, not_2_out, not_3_out, not_4_out);
  or or_1 (or_1_out, comparator_1_eq, comparator_1_lt);
  or or_2 (or_2_out, comparator_2_gt, comparator_2_eq);
  T_Flip_Flop t_ff_1 (.clk(Clock), .T(and_1_out), .Q(t_ff_1_q));  // open: Qn, preset, reset, en
  and and_3 (B_Selector, or_1_out, or_2_out);
  nor nor_1 (Write_Enable, t_ff_1_q, and_2_out);

  assign OP_Out = OP_In;

  // Other names for the same wires on the sheet: Op[3:0] = OP_In
endmodule

module Carry_Lookahead_Generator_1 (
  input  G2,
  input  P2,
  input  in_3,
  input  G1,
  input  P1,
  input  G0,
  input  P0,
  output C3,
  output C2,
  output C1
);

  wire and_1_out, and_2_out, and_3_out, and_4_out, and_5_out, and_6_out;

  and and_1 (and_1_out, P0, in_3);
  and and_2 (and_2_out, P2, G1);
  and and_3 (and_3_out, P2, P1, G0);
  and and_4 (and_4_out, P2, P1, P0, in_3);
  or or_1 (C1, and_1_out, G0);
  or or_2 (C3, and_2_out, G2, and_3_out, and_4_out);
  and and_5 (and_5_out, P1, G0);
  and and_6 (and_6_out, P1, P0, in_3);
  or or_3 (C2, and_5_out, G1, and_6_out);

  // Other names for the same wires on the sheet: C0 = in_3
endmodule

module Carry_Lookahead_Generator_2 (
  input  G5,
  input  P5,
  input  C3,
  input  G4,
  input  P4,
  input  G3,
  input  P3,
  output C6,
  output C5,
  output C4
);

  wire and_1_out, and_2_out, and_3_out, and_4_out, and_5_out, and_6_out;

  and and_1 (and_1_out, P3, C3);
  and and_2 (and_2_out, P5, G4);
  and and_3 (and_3_out, P5, P4, G3);
  and and_4 (and_4_out, P5, P4, P3, C3);
  or or_1 (C4, and_1_out, G3);
  or or_2 (C6, and_2_out, G5, and_3_out, and_4_out);
  and and_5 (and_5_out, P4, G3);
  and and_6 (and_6_out, P4, P3, C3);
  or or_3 (C5, and_5_out, G4, and_6_out);
endmodule

module Carry_Lookahead_Generator_3 (
  input  G8,
  input  P8,
  input  G7,
  input  P7,
  input  C6,
  input  G6,
  input  P6,
  output C9,
  output C8,
  output C7
);

  wire and_1_out, and_2_out, and_3_out, and_4_out, and_5_out, and_6_out;

  and and_1 (and_1_out, P6, C6);
  and and_2 (and_2_out, P8, G7);
  and and_3 (and_3_out, P8, P7, G6);
  and and_4 (and_4_out, P8, P7, P6, C6);
  or or_1 (C7, and_1_out, G6);
  or or_2 (C9, and_2_out, G8, and_3_out, and_4_out);
  and and_5 (and_5_out, P7, G6);
  and and_6 (and_6_out, P7, P6, C6);
  or or_3 (C8, and_5_out, G7, and_6_out);
endmodule

module Full_Adder (
  input  A8,
  input  B8,
  input  A7,
  input  B7,
  input  A6,
  input  B6,
  input  A5,
  input  B5,
  input  A4,
  input  B4,
  input  A3,
  input  B3,
  input  A2,
  input  B2,
  input  A1,
  input  B1,
  input  A0,
  input  B0,
  input  C0,
  output S8,
  output S7,
  output S6,
  output S5,
  output S4,
  output S3,
  output S2,
  output S1,
  output S0
);

  wire and_1_out, and_2_out, and_3_out, and_4_out, and_5_out, and_6_out, and_7_out, and_8_out, and_9_out,
       carry_lookahead_generator_1_1_c1, carry_lookahead_generator_1_1_c2, carry_lookahead_generator_1_1_c3,
       carry_lookahead_generator_2_1_c4, carry_lookahead_generator_2_1_c5, carry_lookahead_generator_2_2_c4,
       carry_lookahead_generator_2_2_c5, carry_lookahead_generator_2_2_c6, P0, P1, P2, P3, P4, P5, P6, P7, P8;

  and and_1 (and_1_out, A8, B8);
  xor xor_1 (P8, A8, B8);
  and and_2 (and_2_out, A7, B7);
  xor xor_2 (P7, A7, B7);
  and and_3 (and_3_out, A6, B6);
  xor xor_3 (P6, A6, B6);
  and and_4 (and_4_out, A2, B2);
  xor xor_4 (P2, A2, B2);
  and and_5 (and_5_out, A1, B1);
  xor xor_5 (P1, A1, B1);
  and and_6 (and_6_out, A0, B0);
  xor xor_6 (P0, A0, B0);
  and and_7 (and_7_out, A5, B5);
  xor xor_7 (P5, A5, B5);
  and and_8 (and_8_out, A4, B4);
  xor xor_8 (P4, A4, B4);
  and and_9 (and_9_out, A3, B3);
  xor xor_9 (P3, A3, B3);
  Carry_Lookahead_Generator_2 carry_lookahead_generator_2_1 (
    .G5(and_1_out), .P5(P8), .G4(and_2_out), .P4(P7), .G3(and_3_out), .P3(P6),
    .C3(carry_lookahead_generator_2_2_c6), .C5(carry_lookahead_generator_2_1_c5),
    .C4(carry_lookahead_generator_2_1_c4));  // open: C6
  Carry_Lookahead_Generator_2 carry_lookahead_generator_2_2 (
    .G5(and_7_out), .P5(P5), .G4(and_8_out), .P4(P4), .G3(and_9_out), .P3(P3),
    .C3(carry_lookahead_generator_1_1_c3), .C6(carry_lookahead_generator_2_2_c6),
    .C5(carry_lookahead_generator_2_2_c5), .C4(carry_lookahead_generator_2_2_c4));
  Carry_Lookahead_Generator_1 carry_lookahead_generator_1_1 (
    .G2(and_4_out), .P2(P2), .G1(and_5_out), .P1(P1), .G0(and_6_out), .P0(P0), .in_3(C0),
    .C3(carry_lookahead_generator_1_1_c3), .C2(carry_lookahead_generator_1_1_c2),
    .C1(carry_lookahead_generator_1_1_c1));
  xor xor_10 (S8, P8, carry_lookahead_generator_2_1_c5);
  xor xor_11 (S7, carry_lookahead_generator_2_1_c4, P7);
  xor xor_12 (S6, P6, carry_lookahead_generator_2_2_c6);
  xor xor_13 (S3, P3, carry_lookahead_generator_1_1_c3);
  xor xor_14 (S2, P2, carry_lookahead_generator_1_1_c2);
  xor xor_15 (S1, carry_lookahead_generator_1_1_c1, P1);
  xor xor_16 (S0, P0, C0);
  xor xor_17 (S5, P5, carry_lookahead_generator_2_2_c5);
  xor xor_18 (S4, carry_lookahead_generator_2_2_c4, P4);
endmodule

module Full_Subtractor (
  input  A8,
  input  B8,
  input  A7,
  input  B7,
  input  A6,
  input  B6,
  input  A5,
  input  B5,
  input  A4,
  input  B4,
  input  A3,
  input  B3,
  input  A2,
  input  B2,
  input  A1,
  input  B1,
  input  A0,
  input  B0,
  input  C0,
  output S8,
  output S7,
  output S6,
  output S5,
  output S4,
  output S3,
  output S2,
  output S1,
  output S0
);

  wire and_1_out, and_2_out, and_3_out, and_4_out, and_5_out, and_6_out, and_7_out, and_8_out, and_9_out,
       B0_t, B1_t, B2_t, B3_t, B4_t, B5_t, B6_t, B7_t, B8_t, carry_lookahead_generator_1_1_c1,
       carry_lookahead_generator_1_1_c2, carry_lookahead_generator_1_1_c3, carry_lookahead_generator_2_1_c4,
       carry_lookahead_generator_2_1_c5, carry_lookahead_generator_2_2_c4, carry_lookahead_generator_2_2_c5,
       carry_lookahead_generator_2_2_c6, P0, P1, P2, P3, P4, P5, P6, P7, P8;

  not not_1 (B8_t, B8);
  not not_2 (B7_t, B7);
  not not_3 (B6_t, B6);
  not not_4 (B5_t, B5);
  not not_5 (B4_t, B4);
  not not_6 (B3_t, B3);
  not not_7 (B2_t, B2);
  not not_8 (B1_t, B1);
  not not_9 (B0_t, B0);
  and and_1 (and_1_out, A8, B8_t);
  xor xor_1 (P8, A8, B8_t);
  and and_2 (and_2_out, A7, B7_t);
  xor xor_2 (P7, A7, B7_t);
  and and_3 (and_3_out, A6, B6_t);
  xor xor_3 (P6, A6, B6_t);
  and and_4 (and_4_out, A2, B2_t);
  xor xor_4 (P2, A2, B2_t);
  and and_5 (and_5_out, A1, B1_t);
  xor xor_5 (P1, A1, B1_t);
  and and_6 (and_6_out, A0, B0_t);
  xor xor_6 (P0, A0, B0_t);
  and and_7 (and_7_out, A5, B5_t);
  xor xor_7 (P5, A5, B5_t);
  and and_8 (and_8_out, A4, B4_t);
  xor xor_8 (P4, A4, B4_t);
  and and_9 (and_9_out, A3, B3_t);
  xor xor_9 (P3, A3, B3_t);
  Carry_Lookahead_Generator_2 carry_lookahead_generator_2_1 (
    .G5(and_1_out), .P5(P8), .G4(and_2_out), .P4(P7), .G3(and_3_out), .P3(P6),
    .C3(carry_lookahead_generator_2_2_c6), .C5(carry_lookahead_generator_2_1_c5),
    .C4(carry_lookahead_generator_2_1_c4));  // open: C6
  Carry_Lookahead_Generator_2 carry_lookahead_generator_2_2 (
    .G5(and_7_out), .P5(P5), .G4(and_8_out), .P4(P4), .G3(and_9_out), .P3(P3),
    .C3(carry_lookahead_generator_1_1_c3), .C6(carry_lookahead_generator_2_2_c6),
    .C5(carry_lookahead_generator_2_2_c5), .C4(carry_lookahead_generator_2_2_c4));
  Carry_Lookahead_Generator_1 carry_lookahead_generator_1_1 (
    .G2(and_4_out), .P2(P2), .G1(and_5_out), .P1(P1), .G0(and_6_out), .P0(P0), .in_3(C0),
    .C3(carry_lookahead_generator_1_1_c3), .C2(carry_lookahead_generator_1_1_c2),
    .C1(carry_lookahead_generator_1_1_c1));
  xor xor_10 (S8, P8, carry_lookahead_generator_2_1_c5);
  xor xor_11 (S7, carry_lookahead_generator_2_1_c4, P7);
  xor xor_12 (S6, P6, carry_lookahead_generator_2_2_c6);
  xor xor_13 (S3, P3, carry_lookahead_generator_1_1_c3);
  xor xor_14 (S2, P2, carry_lookahead_generator_1_1_c2);
  xor xor_15 (S1, carry_lookahead_generator_1_1_c1, P1);
  xor xor_16 (S0, P0, C0);
  xor xor_17 (S5, P5, carry_lookahead_generator_2_2_c5);
  xor xor_18 (S4, carry_lookahead_generator_2_2_c4, P4);
endmodule
